// Logisim project circuito.circ as structural Verilog: 21 circuits, main circuit main
module main (
  output [7:0] out_1
);

  wire caez_flags_1_out_6, caez_flags_1_out_7, caez_flags_1_out_8, caez_flags_1_out_9, control_1_init,
       control_1_out_6, control_1_out_7, control_1_out_8, control_1_out_9, control_1_out_10,
       control_1_out_11, control_1_out_12, control_1_out_13, control_1_out_14, control_1_out_15,
       control_1_out_16, control_1_out_18, control_1_out_19, control_1_out_21, control_1_out_22,
       control_1_out_23, control_1_out_24, control_1_out_25, control_1_out_26, or_1_out, ula_1_carry_out,
       ula_1_equal, ula_1_larger, ula_1_zero;
  wire [2:0] control_1_out_17;
  wire [7:0] bus_1_1_out_3, ir_1_out_3, MAR_q, tmp_1_out_3, ula_1_out_6;

  ULA ula_1 (
    .A(out_1), .B(bus_1_1_out_3), .out_6(ula_1_out_6), .op(control_1_out_17), .carry_out(ula_1_carry_out),
    .larger(ula_1_larger), .equal(ula_1_equal), .zero(ula_1_zero));  // open: carry_in
  ACC ac (.in_2(ula_1_out_6), .out_4(out_1), .s(control_1_out_22), .e(control_1_out_23));
  tmp tmp_1 (.in_1(out_1), .out_3(tmp_1_out_3), .s(control_1_out_7));
  bus_1 bus_1_1 (.in_1(tmp_1_out_3), .out_3(bus_1_1_out_3), .bus1(control_1_out_6));
  CAEZ_Flags caez_flags_1 (
    .C(ula_1_carry_out), .A(ula_1_larger), .E(ula_1_equal), .Z(ula_1_zero), .out_6(caez_flags_1_out_6),
    .out_7(caez_flags_1_out_7), .out_8(caez_flags_1_out_8), .out_9(caez_flags_1_out_9),
    .in_4(control_1_out_21));
  R R0 (.in_1(out_1), .s(control_1_out_8), .e(control_1_out_9), .out_4(out_1));
  R R1 (.in_1(out_1), .s(control_1_out_10), .e(control_1_out_11), .out_4(out_1));
  IR ir_1 (.out_3(ir_1_out_3), .s(control_1_out_26), .in_2(out_1));
  IAR iar_1 (.in_3(out_1), .s(control_1_out_24), .e(control_1_out_25), .out_4(out_1));
  R R2 (.in_1(out_1), .s(control_1_out_12), .e(control_1_out_13), .out_4(out_1));
  R R3 (.in_1(out_1), .s(control_1_out_14), .e(control_1_out_15), .out_4(out_1));
  Control control_1 (
    .out_17(control_1_out_17), .in_1(caez_flags_1_out_6), .in_2(caez_flags_1_out_7),
    .in_3(caez_flags_1_out_8), .in_4(caez_flags_1_out_9), .out_21(control_1_out_21), .out_6(control_1_out_6),
    .out_7(control_1_out_7), .out_8(control_1_out_8), .out_9(control_1_out_9), .out_10(control_1_out_10),
    .out_11(control_1_out_11), .out_12(control_1_out_12), .out_13(control_1_out_13),
    .out_14(control_1_out_14), .out_15(control_1_out_15), .out_16(control_1_out_16),
    .out_22(control_1_out_22), .out_23(control_1_out_23), .out_24(control_1_out_24),
    .out_25(control_1_out_25), .in_5(ir_1_out_3), .out_26(control_1_out_26), .out_18(control_1_out_18),
    .out_19(control_1_out_19), .init(control_1_init));  // open: out_27, out_28, out_29, out_30
  Register MAR (.D(out_1), .Q(MAR_q), .clk(control_1_out_16));  // open: en, clr
  LED led_1 (.in(control_1_init));
  RAM #(.databus("bidir")) ram_1 (
    .addr(MAR_q), .we(control_1_out_18), .oe(control_1_out_19), .clk(or_1_out), .data(out_1));
  or or_1 (or_1_out, control_1_out_18, control_1_out_19);

  // Notes on the sheet:
  //   T
  //   b1
  //   U
  //   L
  //   A
  //   Control
  //   IAR
  //   IR
endmodule

module M_1bit (
  input  in_1,
  input  in_2,
  input  in_3,
  input  in_4,
  input  in_5,
  input  in_6,
  input  in_7,
  input  in_8,
  input  set,
  output out_10,
  output out_11,
  output out_12,
  output out_13,
  output out_14,
  output out_15,
  output out_16,
  output out_17
);

  wire [7:1] main_1_out_1, main_2_out_1, main_3_out_1, main_4_out_1, main_5_out_1, main_6_out_1,
       main_7_out_1, main_8_out_1;

  main main_1 (.out_1({main_1_out_1, out_10}));
  main main_2 (.out_1({main_2_out_1, out_11}));
  main main_3 (.out_1({main_3_out_1, out_12}));
  main main_4 (.out_1({main_4_out_1, out_13}));
  main main_5 (.out_1({main_5_out_1, out_14}));
  main main_6 (.out_1({main_6_out_1, out_15}));
  main main_7 (.out_1({main_7_out_1, out_16}));
  main main_8 (.out_1({main_8_out_1, out_17}));
  // Pins of 1 and 8 bits meet at {main_1_out_1, out_10}
  // Pins of 1 and 8 bits meet at {main_2_out_1, out_11}
  // Pins of 1 and 8 bits meet at {main_3_out_1, out_12}
  // Pins of 1 and 8 bits meet at {main_4_out_1, out_13}
  // Pins of 1 and 8 bits meet at {main_5_out_1, out_14}
  // Pins of 1 and 8 bits meet at {main_6_out_1, out_15}
  // Pins of 1 and 8 bits meet at {main_7_out_1, out_16}
  // Pins of 1 and 8 bits meet at {main_8_out_1, out_17}
endmodule

module B (
  input  in_1,
  input  in_2,
  input  in_3,
  input  in_4,
  input  in_5,
  input  in_6,
  input  in_7,
  input  in_8,
  input  in_9,
  output out_10,
  output out_11,
  output out_12,
  output out_13,
  output out_14,
  output out_15,
  output out_16,
  output out_17
);

  and and_1 (out_10, in_1, in_9);
  and and_2 (out_11, in_2, in_9);
  and and_3 (out_12, in_3, in_9);
  and and_4 (out_13, in_4, in_9);
  and and_5 (out_14, in_5, in_9);
  and and_6 (out_15, in_6, in_9);
  and and_7 (out_16, in_7, in_9);
  and and_8 (out_17, in_8, in_9);
endmodule

module E (
  input  in_1,
  input  in_2,
  input  in_3,
  input  in_4,
  input  in_5,
  input  in_6,
  input  in_7,
  input  in_8,
  input  enable,
  input  set,
  output out_11,
  output out_12,
  output out_13,
  output out_14,
  output out_15,
  output out_16,
  output out_17,
  output out_18
);

  wire m_1bit_1_out_10, m_1bit_1_out_11, m_1bit_1_out_12, m_1bit_1_out_13, m_1bit_1_out_14, m_1bit_1_out_15,
       m_1bit_1_out_16, m_1bit_1_out_17;

  M_1bit m_1bit_1 (
    .in_1(in_1), .in_2(in_2), .in_3(in_3), .in_4(in_4), .in_5(in_5), .in_6(in_6), .in_7(in_7), .in_8(in_8),
    .set(set), .out_10(m_1bit_1_out_10), .out_11(m_1bit_1_out_11), .out_12(m_1bit_1_out_12),
    .out_13(m_1bit_1_out_13), .out_14(m_1bit_1_out_14), .out_15(m_1bit_1_out_15), .out_16(m_1bit_1_out_16),
    .out_17(m_1bit_1_out_17));
  B Ee (
    .in_1(m_1bit_1_out_10), .in_2(m_1bit_1_out_11), .in_3(m_1bit_1_out_12), .in_4(m_1bit_1_out_13),
    .in_5(m_1bit_1_out_14), .in_6(m_1bit_1_out_15), .in_7(m_1bit_1_out_16), .in_8(m_1bit_1_out_17),
    .in_9(enable), .out_10(out_11), .out_11(out_12), .out_12(out_13), .out_13(out_14), .out_14(out_15),
    .out_15(out_16), .out_16(out_17), .out_17(out_18));
endmodule

module R_back (
  input  s,
  input  e,
  input  in_3,
  input  in_4,
  input  in_5,
  input  in_6,
  input  in_7,
  input  in_8
);

  wire [7:0] r_1_out_4;

  R r_1 (.in_1(r_1_out_4), .s(e), .e(s), .out_4(r_1_out_4));
  R r_2 (.in_1(r_1_out_4), .s(in_3), .e(in_6), .out_4(r_1_out_4));
  R r_3 (.in_1(r_1_out_4), .s(in_4), .e(in_7), .out_4(r_1_out_4));
  R r_4 (.in_1(r_1_out_4), .s(in_5), .e(in_8), .out_4(r_1_out_4));
endmodule

module R (
  input  [7:0] in_1,
  input  s,
  input  e,
  output [7:0] out_4
);

  wire [7:0] register_1_q;

  Register register_1 (.D(in_1), .Q(register_1_q), .clk(s));  // open: en, clr
  assign out_4 = e ? register_1_q : 8'bz;  // Controlled_Buffer controlled_buffer_1
endmodule

module Mem (
  input  [7:0] in_1,
  input  s,
  input  write,
  input  leitura,
  input  in_5
);

  wire and_1_out, and_2_out, and_3_out, and_4_out, and_5_out, and_6_out, and_7_out, and_8_out, and_9_out,
       decoder_1_out0, decoder_2_out0, decoder_2_out1, decoder_2_out2;
  wire [7:0] MAR_q, r_1_out_4;

  Register MAR (.D(in_1), .Q(MAR_q), .clk(s));  // open: en, clr
  Decoder #(.enable("false"), .select(4)) decoder_1 (
    .out0(decoder_1_out0), .sel(MAR_q[7:4]));  // open: out1, out2, out3, out4, out5, out6, out7, out8, out9, out10, out11, out12, out13, out14, out15
  and and_1 (and_1_out, decoder_1_out0, decoder_2_out0);
  and and_2 (and_2_out, and_1_out, write);
  and and_3 (and_3_out, and_1_out, leitura);
  R r_1 (.in_1(r_1_out_4), .s(and_2_out), .e(and_3_out), .out_4(r_1_out_4));
  Decoder #(.enable("false"), .select(4)) decoder_2 (
    .out0(decoder_2_out0), .out1(decoder_2_out1), .out2(decoder_2_out2), .sel(MAR_q[3:0]));  // open: out3, out4, out5, out6, out7, out8, out9, out10, out11, out12, out13, out14, out15
  and and_4 (and_4_out, decoder_1_out0, decoder_2_out1);
  and and_5 (and_5_out, and_4_out, write);
  and and_6 (and_6_out, and_4_out, leitura);
  R r_2 (.in_1(r_1_out_4), .s(and_5_out), .e(and_6_out), .out_4(r_1_out_4));
  and and_7 (and_7_out, decoder_1_out0, decoder_2_out2);
  and and_8 (and_8_out, and_7_out, write);
  and and_9 (and_9_out, and_7_out, leitura);
  R r_3 (.in_1(r_1_out_4), .s(and_8_out), .e(and_9_out), .out_4(r_1_out_4));
  Register register_1 (.D(r_1_out_4), .clk(in_5));  // open: en, Q, clr
endmodule

module ULA (
  input  [2:0] op,
  input  [7:0] A,
  input  [7:0] B,
  input  carry_in,
  output carry_out,
  output [7:0] out_6,
  output larger,
  output equal,
  output zero
);

  wire adder_1_cout, left_out_3, right_out_3;
  wire [7:0] adder_1_out, and_1_out, left_out_2, not_1_out, or_1_out, right_out_4, xor_1_out;

  Adder adder_1 (.a(A), .b(B), .out(adder_1_out), .cin(carry_in), .cout(adder_1_cout));
  R_shift right (.in_2(A), .in_1(carry_in), .out_3(right_out_3), .out_4(right_out_4));
  L_shift left (.in_1(A), .out_3(left_out_3), .out_2(left_out_2));
  assign not_1_out = ~A;  // NOT_Gate not_1, 8 bits wide
  Comparator comparator_1 (.a(A), .b(B), .gt(larger), .eq(equal));  // open: lt
  assign and_1_out = A & B;  // AND_Gate and_1, 8 bits wide
  assign or_1_out = A | B;  // OR_Gate or_1, 8 bits wide
  assign xor_1_out = A ^ B;  // XOR_Gate xor_1, 8 bits wide
  Multiplexer #(.select(3)) multiplexer_1 (
    .in0(adder_1_cout), .in1(right_out_3), .in2(left_out_3), .in3(1'b0), .in4(1'b0), .in5(1'b0), .in6(1'b0),
    .in7(1'b0), .out(carry_out), .sel(op));
  Multiplexer #(.select(3), .width(8)) multiplexer_2 (
    .in0(adder_1_out), .in1(right_out_4), .in2(left_out_2), .in3(not_1_out), .in4(and_1_out), .in5(or_1_out),
    .in6(xor_1_out), .out(out_6), .sel(op));  // open: in7
  Comparator comparator_2 (.a(out_6), .b({8{1'b0}}), .eq(zero));  // open: gt, lt

  // Notes on the sheet:
  //   A > B
endmodule

module L_shift (
  input  [7:0] in_1,
  output [7:0] out_2,
  output out_3
);


  assign out_2 = {in_1[6:0], 1'b0};
  assign out_3 = in_1[7];
endmodule

module R_shift (
  input  in_1,
  input  [7:0] in_2,
  output out_3,
  output [7:0] out_4
);


  assign out_3 = in_2[0];
  assign out_4 = {in_1, in_2[7:1]};
endmodule

module comp_2bits (
  input  in_1,
  input  b__eh_maior,
  input  a,
  input  b,
  output c,
  output out_6,
  output a__eh_maior
);

  wire and_2_out, not_1_out;

  xor xor_1 (c, a, b);
  not not_1 (not_1_out, c);
  and and_1 (out_6, not_1_out, in_1);
  and and_2 (and_2_out, a, in_1, c);
  or or_1 (a__eh_maior, and_2_out, b__eh_maior);

  // Notes on the sheet:
  //   bits anteriores iguais
  //   bits continuam iguais
endmodule

module comp_8bits (
  input  in_1,
  input  in_2,
  input  [7:0] in_3,
  input  [7:0] in_4,
  output [7:0] out_5,
  output equal,
  output a_maior
);

  wire comp_2bits_1_a__eh_maior, comp_2bits_1_out_6, comp_2bits_2_a__eh_maior, comp_2bits_2_out_6,
       comp_2bits_3_a__eh_maior, comp_2bits_3_out_6, comp_2bits_4_a__eh_maior, comp_2bits_4_out_6,
       comp_2bits_5_a__eh_maior, comp_2bits_5_out_6, comp_2bits_6_a__eh_maior, comp_2bits_6_out_6,
       comp_2bits_7_a__eh_maior, comp_2bits_7_out_6;

  comp_2bits comp_2bits_1 (
    .a(in_3[7]), .b(in_4[7]), .in_1(in_1), .b__eh_maior(in_2), .out_6(comp_2bits_1_out_6),
    .a__eh_maior(comp_2bits_1_a__eh_maior), .c(out_5[0]));
  comp_2bits comp_2bits_2 (
    .a(in_3[6]), .b(in_4[6]), .in_1(comp_2bits_1_out_6), .b__eh_maior(comp_2bits_1_a__eh_maior),
    .out_6(comp_2bits_2_out_6), .a__eh_maior(comp_2bits_2_a__eh_maior), .c(out_5[1]));
  comp_2bits comp_2bits_3 (
    .a(in_3[5]), .b(in_4[5]), .in_1(comp_2bits_2_out_6), .b__eh_maior(comp_2bits_2_a__eh_maior),
    .out_6(comp_2bits_3_out_6), .a__eh_maior(comp_2bits_3_a__eh_maior), .c(out_5[2]));
  comp_2bits comp_2bits_4 (
    .a(in_3[4]), .b(in_4[4]), .in_1(comp_2bits_3_out_6), .b__eh_maior(comp_2bits_3_a__eh_maior),
    .out_6(comp_2bits_4_out_6), .a__eh_maior(comp_2bits_4_a__eh_maior), .c(out_5[3]));
  comp_2bits comp_2bits_5 (
    .a(in_3[3]), .b(in_4[3]), .in_1(comp_2bits_4_out_6), .b__eh_maior(comp_2bits_4_a__eh_maior),
    .out_6(comp_2bits_5_out_6), .a__eh_maior(comp_2bits_5_a__eh_maior), .c(out_5[4]));
  comp_2bits comp_2bits_6 (
    .a(in_3[2]), .b(in_4[2]), .in_1(comp_2bits_5_out_6), .b__eh_maior(comp_2bits_5_a__eh_maior),
    .out_6(comp_2bits_6_out_6), .a__eh_maior(comp_2bits_6_a__eh_maior), .c(out_5[5]));
  comp_2bits comp_2bits_7 (
    .a(in_3[1]), .b(in_4[1]), .in_1(comp_2bits_6_out_6), .b__eh_maior(comp_2bits_6_a__eh_maior),
    .out_6(comp_2bits_7_out_6), .a__eh_maior(comp_2bits_7_a__eh_maior), .c(out_5[6]));
  comp_2bits comp_2bits_8 (
    .a(in_3[0]), .b(in_4[0]), .in_1(comp_2bits_7_out_6), .b__eh_maior(comp_2bits_7_a__eh_maior),
    .out_6(equal), .a__eh_maior(a_maior), .c(out_5[7]));

  // Notes on the sheet:
  //   a
  //   b
  //   c
endmodule

module tmp (
  input  [7:0] in_1,
  input  s,
  output [7:0] out_3
);

  Register register_1 (.D(in_1), .Q(out_3), .clk(s));  // open: en, clr
endmodule

module bus_1 (
  input  [7:0] in_1,
  input  bus1,
  output [7:0] out_3
);

  Multiplexer #(.width(8)) multiplexer_1 (.in0(in_1), .in1(8'h1), .out(out_3), .sel(bus1));
endmodule

module ACC (
  input  s,
  input  [7:0] in_2,
  input  e,
  output [7:0] out_4
);

  wire [7:0] register_1_q;

  Register register_1 (.D(in_2), .Q(register_1_q), .clk(s));  // open: en, clr
  assign out_4 = e ? register_1_q : 8'bz;  // Controlled_Buffer controlled_buffer_1
endmodule

module Clk (
  output clk_o,
  output e,
  output s
);

  wire clk_d_out;

  Clock #(.highDuration(2), .lowDuration(2)) clk (.out(clk_o));
  Clock #(.highDuration(2), .lowDuration(2), .phaseOffset(3)) clk_d (.out(clk_d_out));
  or or_1 (e, clk_o, clk_d_out);
  and and_1 (s, clk_o, clk_d_out);
endmodule

module Control (
  input  in_1,
  input  in_2,
  input  in_3,
  input  in_4,
  input  [7:0] in_5,
  output out_6,
  output out_7,
  output out_8,
  output out_9,
  output out_10,
  output out_11,
  output out_12,
  output out_13,
  output out_14,
  output out_15,
  output out_16,
  output [2:0] out_17,
  output out_18,
  output out_19,
  output init,
  output out_21,
  output out_22,
  output out_23,
  output out_24,
  output out_25,
  output out_26,
  output out_27,
  output out_28,
  output out_29,
  output out_30
);

  wire A_out, and_5_out, and_6_out, and_7_out, and_8_out, and_9_out, and_10_out, and_11_out, and_12_out,
       and_16_out, and_17_out, and_18_out, and_19_out, and_20_out, and_21_out, and_22_out, and_23_out,
       and_24_out, and_25_out, and_26_out, and_27_out, and_28_out, and_29_out, and_30_out, and_31_out,
       and_32_out, and_33_out, and_34_out, and_35_out, and_36_out, and_37_out, and_38_out, and_39_out,
       and_40_out, and_41_out, and_42_out, and_43_out, C_out, clk_1_clk_o, clk_e, clk_s, decoder_1_out0,
       decoder_1_out1, decoder_1_out2, decoder_1_out3, decoder_2_out0, decoder_2_out1, decoder_2_out2,
       decoder_2_out3, decoder_3_out0, decoder_3_out1, decoder_3_out2, decoder_3_out3, decoder_3_out4,
       decoder_3_out5, decoder_3_out6, decoder_3_out7, decoder_4_out0, decoder_4_out1, decoder_4_out2,
       decoder_4_out3, E_out, not_1_out, not_2_out, not_3_out, or_6_out, or_7_out, or_8_out, or_9_out,
       or_10_out, or_11_out, or_12_out, or_13_out, or_14_out, or_15_out, or_16_out, stepper_1_out_3,
       stepper_1_out_4, stepper_1_out_5, stepper_1_out_6, stepper_1_out_7, stepper_1_out_8, Z_out;

  Clk clk_1 (.clk_o(clk_1_clk_o), .e(clk_e), .s(clk_s));
  or or_1 (out_9, and_5_out, and_9_out);
  or or_2 (out_11, and_6_out, and_10_out);
  or or_3 (out_13, and_7_out, and_11_out);
  or or_4 (out_15, and_8_out, and_12_out);
  and and_1 (out_25, or_6_out, clk_e);
  buf and_2 (out_19, or_7_out);  // AND_Gate
  and and_3 (out_23, or_8_out, clk_e);
  and and_4 (out_29, and_39_out, clk_e);
  and and_5 (and_5_out, clk_e, or_9_out, decoder_2_out0);
  and and_6 (and_6_out, clk_e, or_9_out, decoder_2_out1);
  and and_7 (and_7_out, clk_e, or_9_out, decoder_2_out2);
  and and_8 (and_8_out, clk_e, or_9_out, decoder_2_out3);
  and and_9 (and_9_out, clk_e, or_10_out, decoder_1_out0);
  and and_10 (and_10_out, clk_e, or_10_out, decoder_1_out1);
  and and_11 (and_11_out, clk_e, or_10_out, decoder_1_out2);
  and and_12 (and_12_out, clk_e, or_10_out, decoder_1_out3);
  or or_5 (out_6, stepper_1_out_3, and_31_out, and_30_out, and_27_out);
  or or_6 (or_6_out, stepper_1_out_3, and_27_out, and_29_out, and_30_out);
  or or_7 (or_7_out, stepper_1_out_4, and_43_out, and_37_out, and_36_out, and_34_out);
  or or_8 (or_8_out, stepper_1_out_5, and_38_out, and_42_out, and_41_out);
  or or_9 (or_9_out, and_24_out, and_35_out, and_28_out, and_32_out);
  or or_10 (or_10_out, and_26_out, and_25_out, and_33_out);
  Decoder #(.enable("false"), .select(2)) decoder_1 (
    .out0(decoder_1_out0), .out1(decoder_1_out1), .out2(decoder_1_out2), .out3(decoder_1_out3),
    .sel(in_5[3:2]));
  Decoder #(.enable("false"), .select(2)) decoder_2 (
    .out0(decoder_2_out0), .out1(decoder_2_out1), .out2(decoder_2_out2), .out3(decoder_2_out3),
    .sel(in_5[1:0]));
  and and_13 (out_17[0], stepper_1_out_7, in_5[7], in_5[4]);
  and and_14 (out_17[1], stepper_1_out_7, in_5[7], in_5[5]);
  and and_15 (out_17[2], stepper_1_out_7, in_5[7], in_5[6]);
  Decoder #(.enable("false"), .select(3)) decoder_3 (
    .out0(decoder_3_out0), .out1(decoder_3_out1), .out2(decoder_3_out2), .out3(decoder_3_out3),
    .out4(decoder_3_out4), .out5(decoder_3_out5), .out6(decoder_3_out6), .out7(decoder_3_out7),
    .sel(in_5[6:4]));
  not not_1 (not_1_out, in_5[7]);
  and and_16 (and_16_out, not_1_out, decoder_3_out0);
  and and_17 (and_17_out, not_1_out, decoder_3_out1);
  and and_18 (and_18_out, not_1_out, decoder_3_out2);
  and and_19 (and_19_out, not_1_out, decoder_3_out3);
  and and_20 (and_20_out, not_1_out, decoder_3_out4);
  and and_21 (and_21_out, not_1_out, decoder_3_out5);
  and and_22 (and_22_out, not_1_out, decoder_3_out6);
  and and_23 (and_23_out, not_1_out, decoder_3_out7);
  and and_24 (and_24_out, stepper_1_out_6, in_5[7]);
  and and_25 (and_25_out, stepper_1_out_6, and_16_out);
  and and_26 (and_26_out, stepper_1_out_6, and_17_out);
  and and_27 (and_27_out, stepper_1_out_6, and_18_out);
  and and_28 (and_28_out, stepper_1_out_6, and_19_out);
  and and_29 (and_29_out, stepper_1_out_6, and_20_out);
  and and_30 (and_30_out, stepper_1_out_6, and_21_out);
  and and_31 (and_31_out, stepper_1_out_6, and_22_out);
  and and_32 (and_32_out, stepper_1_out_6, and_23_out, in_5[3]);
  not not_2 (not_2_out, in_5[3]);
  and C (C_out, in_5[3], in_1);
  and A (A_out, in_5[2], in_2);
  and E (E_out, in_5[1], in_3);
  and Z (Z_out, in_5[0], in_4);
  and and_33 (and_33_out, stepper_1_out_7, in_5[7]);
  and and_34 (and_34_out, stepper_1_out_7, and_16_out);
  and and_35 (and_35_out, stepper_1_out_7, and_17_out);
  and and_36 (and_36_out, stepper_1_out_7, and_18_out);
  and and_37 (and_37_out, stepper_1_out_7, and_20_out);
  and and_38 (and_38_out, stepper_1_out_7, and_21_out);
  and and_39 (and_39_out, stepper_1_out_7, and_23_out, not_2_out);
  or or_11 (or_11_out, C_out, A_out, E_out, Z_out);
  and and_40 (and_40_out, in_5[4], in_5[5], in_5[6]);
  not not_3 (not_3_out, and_40_out);
  stepper stepper_1 (
    .clk_o(clk_1_clk_o), .out_3(stepper_1_out_3), .out_4(stepper_1_out_4), .out_5(stepper_1_out_5),
    .out_6(stepper_1_out_6), .out_7(stepper_1_out_7), .out_8(stepper_1_out_8), .init_cycle(init));
  and and_41 (and_41_out, stepper_1_out_8, in_5[7], not_3_out);
  and and_42 (and_42_out, stepper_1_out_8, and_18_out);
  and and_43 (and_43_out, stepper_1_out_8, and_21_out, or_11_out);
  or or_12 (or_12_out, stepper_1_out_3, and_27_out, and_30_out, and_25_out, and_26_out, and_29_out);
  or or_13 (or_13_out, stepper_1_out_5, and_28_out, and_37_out, and_38_out, and_42_out, and_43_out);
  or or_14 (or_14_out, stepper_1_out_3, and_27_out, and_30_out, and_33_out);
  or or_15 (or_15_out, and_31_out, and_33_out);
  or or_16 (or_16_out, and_34_out, and_41_out, and_36_out, and_39_out);
  Decoder #(.enable("false"), .select(2)) decoder_4 (
    .out0(decoder_4_out0), .out1(decoder_4_out1), .out2(decoder_4_out2), .out3(decoder_4_out3),
    .sel(in_5[1:0]));
  and and_44 (out_26, clk_s, stepper_1_out_4);
  and and_45 (out_16, clk_s, or_12_out);
  and and_46 (out_24, clk_s, or_13_out);
  and and_47 (out_22, clk_s, or_14_out);
  and and_48 (out_18, clk_s, and_35_out);
  and and_49 (out_7, clk_s, and_24_out);
  and and_50 (out_21, clk_s, or_15_out);
  and and_51 (out_30, clk_s, and_32_out);
  and and_52 (out_8, decoder_4_out0, or_16_out, clk_s);
  and and_53 (out_10, decoder_4_out1, or_16_out, clk_s);
  and and_54 (out_12, decoder_4_out2, or_16_out, clk_s);
  and and_55 (out_14, decoder_4_out3, or_16_out, clk_s);

  assign out_27 = in_5[3];

  // Other names for the same wires on the sheet: from_IR[7:0] = in_5; ACC_e = out_23; ACC_s = out_22; b1 = out_6;
  //   carry_out = in_1; Data_address = out_28; equal = in_3; flag = out_21; Data_adress = in_5[2]; I_O = in_5[3];
  //   IAR_e = out_25; IAR_s = out_24; IO_e = out_29; IO_s = out_30; IR_s = out_26; larger = in_2; mar_s = out_16;
  //   r0e = out_9; r0s = out_8; r1e = out_11; r1s = out_10; r2e = out_13; r2s = out_12; r3e = out_15; r3s = out_14;
  //   RAM_e = out_19; RAM_s = out_18; tmp = out_7; ULA[2:0] = out_17; zero = in_4

  // Notes on the sheet:
  //   clk
  //   stepper
endmodule

module stepper (
  input  clk_o,
  output init_cycle,
  output out_3,
  output out_4,
  output out_5,
  output out_6,
  output out_7,
  output out_8
);

  wire [2:0] counter_1_q;

  Counter #(.max('h6), .width(3)) counter_1 (
    .D(3'b000), .Q(counter_1_q), .clk(clk_o));  // open: load, count, carry, up, clr
  Decoder #(.select(3)) decoder_1 (
    .out0(init_cycle), .out1(out_3), .out2(out_4), .out3(out_5), .out4(out_6), .out5(out_7), .out6(out_8),
    .sel(counter_1_q));  // open: out7, en
endmodule

module IR (
  input  s,
  input  [7:0] in_2,
  output [7:0] out_3
);

  Register register_1 (.D(in_2), .Q(out_3), .clk(s));  // open: en, clr
endmodule

module IAR (
  input  s,
  input  e,
  input  [7:0] in_3,
  output [7:0] out_4
);

  wire [7:0] register_1_q;

  assign out_4 = e ? register_1_q : 8'bz;  // Controlled_Buffer controlled_buffer_1
  Register register_1 (.D(in_3), .Q(register_1_q), .clk(s));  // open: en, clr
endmodule

module CAEZ_Flags (
  input  C,
  input  A,
  input  E,
  input  in_4,
  input  Z,
  output out_6,
  output out_7,
  output out_8,
  output out_9
);

  Register #(.width(4)) register_1 (.D({Z, E, A, C}), .Q({out_9, out_8, out_7, out_6}), .clk(in_4));  // open: en, clr
endmodule
